// Digital circuit H_counter.dig as structural Verilog
module H_counter (
  input  E_C,
  input  [8:0] RES,
  input  [8:0] FP,
  input  [8:0] SP,
  input  [8:0] BP,
  input  Clk,
  output H_blank,
  output H_sync,
  output ENABLE,
  output D0,
  output D1,
  output D2,
  output D3,
  output D4,
  output D5,
  output D6,
  output D7,
  output D8
);

  wire comparator_1_eq, comparator_2_eq, comparator_3_eq;

  Counter #(.Bits(9)) Contatore_Orizzontale (
    .en(E_C), .C(Clk), .clr(ENABLE), .out({D8, D7, D6, D5, D4, D3, D2, D1, D0}));  // open: ovf
  Comparator #(.Bits(9)) comparator_1 (
    .a({D8, D7, D6, D5, D4, D3, D2, D1, D0}), .b(RES), .eq(comparator_1_eq));  // open: gt, lt
  Comparator #(.Bits(9)) comparator_2 (
    .a({D8, D7, D6, D5, D4, D3, D2, D1, D0}), .b(FP), .eq(comparator_2_eq));  // open: gt, lt
  Comparator #(.Bits(9)) comparator_3 (
    .a({D8, D7, D6, D5, D4, D3, D2, D1, D0}), .b(SP), .eq(comparator_3_eq));  // open: gt, lt
  Comparator #(.Bits(9)) comparator_4 (.a({D8, D7, D6, D5, D4, D3, D2, D1, D0}), .b(BP), .eq(ENABLE));  // open: gt, lt
  RS_FF_AS rs_ff_as_1 (.S(ENABLE), .R(comparator_1_eq), .nQ(H_blank));  // open: Q
  RS_FF_AS rs_ff_as_2 (.S(comparator_2_eq), .R(comparator_3_eq), .Q(H_sync));  // open: nQ
  // Pins of 1 and 9 bits meet at RES
  // Pins of 1 and 9 bits meet at FP
  // Pins of 1 and 9 bits meet at SP
  // Pins of 1 and 9 bits meet at BP
endmodule
