// Digital circuit VGA_schem.dig as structural Verilog
module VGA_schem (
  input  clk,
  output out_2,
  output [5:0] out_3,
  output [4:0] out_4
);

  wire and_1_out, and_2_out, bussplitter_1_d0, bussplitter_1_d1, bussplitter_1_d2, bussplitter_1_d3,
       bussplitter_1_d4, bussplitter_1_d5, bussplitter_2_d0, bussplitter_2_d1, bussplitter_2_d2,
       bussplitter_2_d3, bussplitter_2_d4, bussplitter_3_d0, bussplitter_3_d1, bussplitter_3_d2,
       bussplitter_3_d3, bussplitter_4_d0, bussplitter_4_d1, comparator_1_eq, comparator_2_eq, nand_1_out,
       undriven;
  wire [3:0] bussplitter_3_d, bussplitter_4_d;
  wire [9:0] rom_1_d;

  Counter #(.Bits(2)) Div4 (.en(1'b1), .C(clk), .clr(1'b0));  // open: out, ovf
  H_counter h_counter_1 ();  // open: E_C, Clk, RES, FP, SP, BP, H_blank, H_sync, ENABLE, D0, D1, D2, D3, D4, D5, D6, D7, D8
  BusSplitter #(.Bits(6)) bussplitter_1 (
    .D(out_3), .OE(1'b0), .D0(bussplitter_1_d0), .D1(bussplitter_1_d1), .D2(bussplitter_1_d2),
    .D3(bussplitter_1_d3), .D4(bussplitter_1_d4), .D5(bussplitter_1_d5));
  BusSplitter #(.Bits(5)) bussplitter_2 (
    .D(out_4), .OE(1'b0), .D0(bussplitter_2_d0), .D1(bussplitter_2_d1), .D2(bussplitter_2_d2),
    .D3(bussplitter_2_d3), .D4(bussplitter_2_d4));
  BusSplitter #(.Bits(4)) bussplitter_3 (
    .D(bussplitter_3_d), .OE(1'b0), .D0(bussplitter_3_d0), .D1(bussplitter_3_d1), .D2(bussplitter_3_d2),
    .D3(bussplitter_3_d3));
  BusSplitter #(.Bits(4)) bussplitter_4 (
    .D(bussplitter_4_d), .OE(1'b0), .D0(bussplitter_4_d0), .D1(bussplitter_4_d1));  // open: D2, D3
  // NAnd nand_1 has open pins: In_1=open, In_2=open, out=nand_1_out
  ROM #(.AddrBits(4), .Bits(10)) rom_1 (.A(bussplitter_3_d), .sel(nand_1_out), .D(rom_1_d));
  Comparator #(.Bits(6)) comparator_1 (.a(out_3), .b(6'b010100), .eq(comparator_1_eq));  // open: gt, lt
  Comparator #(.Bits(5)) comparator_2 (.a(out_4), .b({5{1'b0}}), .eq(comparator_2_eq));  // open: gt, lt
  Multiplexer #(.Selector_Bits(4)) multiplexer_1 (
    .sel(bussplitter_4_d), .in_0(rom_1_d[0]), .in_1(rom_1_d[1]), .in_2(rom_1_d[2]), .in_3(rom_1_d[3]),
    .in_4(rom_1_d[4]), .in_5(rom_1_d[5]), .in_6(rom_1_d[6]), .in_7(rom_1_d[7]), .in_8(rom_1_d[8]),
    .in_9(rom_1_d[9]), .in_10(1'b0), .in_11(1'b0), .in_12(1'b0), .in_13(1'b0), .in_14(1'b0), .in_15(1'b0),
    .out(out_2));
  and and_1 (and_1_out, comparator_1_eq, comparator_2_eq);
  VGA vga_1 (.R(and_2_out), .G(1'b0), .B(1'b0), .V(undriven), .C(clk));  // open: H
  and and_2 (and_2_out, and_1_out, out_2);

  // Notes on the sheet:
  //   clk: Hz: 2147483647
  //   contents of rom_1 (hex, n*v repeats v):
  //   0,30,84,84,84,fc,84,84,8*0,5*b45,b55,c55,c55,c65,7*c66,10*d66
  //   ,16*c66,c65,c55,b56,b55,b45,b56,d77,e87,e87,d86,d86,d86,d87,d86,d86
  //   ,d76,d86,e86,e86,d86,d86,fc9,fd9,fc9,d86,a44,5*b56,b55,7*c55,b55
  //   ,c76,d77,28*0,e87,e87,e86,e86,e86,d86,e86,e87,e97,e87,e86,d66
  //   ,a45,934,a45,6*b45,b55,c55,c55,c55,c65,c65,c66,c66,c66,12*d66
  //   ,c66,c65,c65,c65,6*c66,5*c65,c66,c66,c56,c55,b55,b45,b55,c66,d77
  //   ,e87,d86,d86,d86,d87,e86,e86,e86,5*d86,ea7,fc9,fda,fb9,b66,a45
  //   ,5*b55,4*c55,c65,c65,c66,b56,834,613,28*0,4*e86,d86,e86,e87,e97,e97
  //   ,e86,e86,d66,a44,934,a45,4*b45,a44,b45,b55,4*c55,4*c65,12*d66
  //   ,4*c65,5*c66,6*c65,c66,c66,c56,c56,b55,b45,b45,c55,d76,5*e87,4*e86
  //   ,d76,d76,d76,e76,d76,eb8,fd9,fda,eb9,7*b55,c55,c56,c55,c65,c66
  //   ,a55,723,513,514,28*0,6*e86,e87,4*e86,d66,b44,a34,a35,4*b45,b44
  //   ,b45,5*c55,c65,d65,c65,c65,d65,8*d66,d65,d65,4*c65,c55,c65,c66
  //   ,d66,d66,c66,c66,5*c55,c66,4*c56,b55,b45,b55,c66,d77,4*e87,4*e86
  //   ,d86,4*d76,d86,fb8,fda,fda,da8,a54,b55,b55,b55,c55,b55,c55,c66,c66
  //   ,c67,944,613,513,514,614,28*0,5*e86,e87,e87,e86,e86,e86,e76,d65
  //   ,a44,a34,a34,4*b45,b44,b45,6*c55,d55,c55,c55,d55,6*d65,d66,d66
  //   ,8*c55,c65,c65,d66,d66,c66,5*c55,5*c56,b55,b45,b56,c66,d77,e87,e87,e87
  //   ,d86,5*e86,d86,d86,d86,d76,d75,d96,fc9,fd9,fd9,d97,b55,b55,b56
  //   ,c56,b55,c56,c66,b56,724,613,514,614,513,613,28*0,7*e87,4*e86
  //   ,d65,a44,934,a34,b45,b45,b44,b44,b44,b45,8*c55,9*d55,d66,d55,8*c55
  //   ,d55,d66,c66,c66,c55,c56,c56,d56,d55,c55,c55,c55,c56,c55,b55,b45
  //   ,b55,c66,d77,d77,d87,d87,d87,e87,6*e86,d86,d76,d76,d75,ea7,fc9
  //   ,fda,fca,c76,a45,b55,c55,c55,c66,a45,613,513,614,614,614,513,613
  //   ,28*0,4*e87,7*e86,d66,a44,934,a44,a45,b45,b44,b44,b44,b45,7*c55
  //   ,d55,d55,d56,d55,c55,c55,d55,d56,d56,c56,c56,c56,c66,c66,c66,c77,c77,c77
  //   ,c76,b65,b55,c65,7*c56,5*c55,b55,b45,b55,c66,d76,d76,d77,d87,d87,d87
  //   ,d86,d76,e86,e86,e76,e76,d76,d76,d76,d75,d75,ea8,fc9,fda,fc9,a65
  //   ,b55,b55,b56,834,613,513,513,624,614,614,513,513,28*0,e86,e86
  //   ,e87,e87,d76,d75,e76,4*e86,d66,a44,934,a44,a45,b45,b45,b45,b44
  //   ,b45,7*c55,d55,d55,d56,d66,c55,c56,c66,c66,c66,c67,c77,c77,c77
  //   ,c88,d98,d99,5*da9,c98,c77,b55,c55,d56,d56,c56,c66,4*c55,b55,b45,b45,b45
  //   ,c66,d66,d76,d76,d77,d77,d77,d76,d76,e76,e76,4*d76,d66,d65,d75
  //   ,d86,fb9,fda,fda,eb9,b65,b55,724,503,514,514,614,614,614,513,513,513
  //   ,28*0,e86,e97,e87,e76,c65,d65,e76,4*e86,d66,a34,934,a34,a45,b45
  //   ,a45,b45,b45,b45,7*c55,d55,c55,d55,c56,d66,d67,c66,c66,c67,c77,c77,c77
  //   ,c88,c88,c98,c99,c99,ca9,ca9,da9,daa,dba,eba,da9,c77,b55,c56,c56,c56
  //   ,4*c55,b55,b45,b45,b45,c66,d66,d76,d76,d76,d77,d76,e77,6*d76,d66,d66,d66
  //   ,d65,d75,d86,fc9,fda,fdb,da9,613,503,514,514,614,614,614,514,614
  //   ,513,513,28*0,e96,f97,e76,d65,a33,c55,e76,e87,e86,e86,e86,d65
  //   ,a34,934,934,a34,a45,a44,a45,b45,b45,b45,8*c55,d66,c55,c66,c66
  //   ,b56,b56,b66,c67,b67,c77,c77,c78,c88,c98,d99,da9,da9,da9,db9,dba,dba,dba
  //   ,eba,da9,c77,a55,b55,c55,c55,c55,b55,4*b45,c56,d77,d77,12*d76
  //   ,d66,d66,d76,d76,d65,e97,fca,fcb,966,513,514,514,614,614,514,513
  //   ,614,513,614,513,28*0,f97,e87,d66,b44,a33,c55,e76,4*e86,d65,a34
  //   ,923,934,4*a45,a44,b45,b45,b45,6*c55,d66,c55,b45,b55,b55,b56,b66
  //   ,4*c66,c77,c77,c77,c88,d98,da9,da9,da9,dba,dba,eba,eba,dba,dba
  //   ,ecb,daa,a66,a44,5*b45,a45,b45,c56,e77,e77,d76,d76,d66,c66,d66
  //   ,d76,d76,d66,9*d76,d77,d88,844,513,514,514,613,613,613,614,514
  //   ,513,624,614,624,28*0,f86,d76,b45,934,a34,c65,e76,e86,e96,e86
  //   ,e76,d65,a34,923,934,a44,a45,a45,a45,a44,b45,b45,b45,6*c55,d66
  //   ,c55,b45,b55,b55,c55,c56,b66,b66,c66,c66,c67,c77,c77,c87,d98,da9,da9
  //   ,dba,daa,4*dba,dbb,dcb,ecb,edc,ebb,a66,a45,b45,b45,a45,a45,b45
  //   ,c56,e76,e77,e76,e77,d66,b45,b55,c66,e76,e65,e76,d76,d66,5*d76
  //   ,e77,c67,723,513,513,514,514,513,513,614,614,514,624,624,734,c77
  //   ,28*0,e76,c55,a34,934,a34,c65,e76,e87,e97,e86,e76,d65,a34,924
  //   ,934,a44,a45,a45,a45,a44,b45,b45,b45,7*c55,b45,b55,c55,c55,b55,b55
  //   ,b56,b66,c66,c66,c67,c77,c77,c77,d88,d99,da9,dba,da9,da9,dba,dbb
  //   ,ecb,ecc,ecb,ecb,ecb,fdc,ecb,955,934,a35,b45,a45,b45,c56,d76,e76,e76
  //   ,e77,d66,b45,823,a45,d66,e76,e76,6*d76,d77,d77,723,513,513,614,614,614
  //   ,613,613,514,514,625,735,845,c77,c77,28*0,c55,a33,a34,a34,a34
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endmodule
