// Digital circuit V_counter.dig as structural Verilog
module V_counter (
  input  [9:0] RES,
  input  [9:0] FP,
  input  [9:0] SC,
  input  [9:0] BP,
  input  EN,
  input  Clk,
  output V_blank,
  output V_sync,
  output D0,
  output D1,
  output D2,
  output D3,
  output D4,
  output D5,
  output D6,
  output D7,
  output D8,
  output D9
);

  wire comparator_1_eq, comparator_2_eq, comparator_3_eq, comparator_4_eq;

  Counter #(.Bits(10)) Contatore_Verticale (
    .en(EN), .C(Clk), .clr(comparator_4_eq), .out({D9, D8, D7, D6, D5, D4, D3, D2, D1, D0}));  // open: ovf
  Comparator #(.Bits(10)) comparator_1 (
    .a({D9, D8, D7, D6, D5, D4, D3, D2, D1, D0}), .b(RES), .eq(comparator_1_eq));  // open: gt, lt
  Comparator #(.Bits(10)) comparator_2 (
    .a({D9, D8, D7, D6, D5, D4, D3, D2, D1, D0}), .b(FP), .eq(comparator_2_eq));  // open: gt, lt
  Comparator #(.Bits(10)) comparator_3 (
    .a({D9, D8, D7, D6, D5, D4, D3, D2, D1, D0}), .b(SC), .eq(comparator_3_eq));  // open: gt, lt
  Comparator #(.Bits(10)) comparator_4 (
    .a({D9, D8, D7, D6, D5, D4, D3, D2, D1, D0}), .b(BP), .eq(comparator_4_eq));  // open: gt, lt
  RS_FF_AS rs_ff_as_1 (.S(comparator_4_eq), .R(comparator_1_eq), .nQ(V_blank));  // open: Q
  RS_FF_AS rs_ff_as_2 (.S(comparator_2_eq), .R(comparator_3_eq), .Q(V_sync));  // open: nQ
endmodule
